// Logisim project logisimOb1 .circ as structural Verilog: 1 circuit, main circuit main
module main (
  input  a0,
  input  a1,
  input  b0,
  input  b1,
  input  Decodificadores,
  input  in_6,
  input  in_7
);

  wire and_1_out, and_3_out, nand_1_out, nor_1_out, not_1_out, not_2_out, not_3_out, not_4_out, or_1_out;

  not not_1 (not_1_out, Decodificadores);
  not not_2 (not_2_out, in_6);
  not not_3 (not_3_out, in_7);
  not not_4 (not_4_out, a0);
  and and_1 (and_1_out, b0, b0, a0);
  or or_1 (or_1_out, b0, a0);
  nand nand_1 (nand_1_out, a0, b0);
  nor nor_1 (nor_1_out, a0, b0);
  // AND_Gate and_2 has open pins: in0=not_1_out, in2=not_2_out, in4=not_3_out, out=open
  and and_3 (and_3_out, not_1_out, not_2_out, in_7);
  // AND_Gate and_4 has open pins: in0=not_1_out, in2=in_6, in4=not_3_out, out=open
  // AND_Gate and_5 has open pins: in0=not_1_out, in2=in_6, in4=in_7, out=open
  // AND_Gate and_6 has open pins: in0=Decodificadores, in2=not_2_out, in4=not_3_out, out=open
  // AND_Gate and_7 has open pins: in0=Decodificadores, in2=not_2_out, in4=in_7, out=open
  // AND_Gate and_8 has open pins: in0=Decodificadores, in2=in_6, in4=not_3_out, out=open
  // AND_Gate and_9 has open pins: in0=Decodificadores, in2=in_6, in4=in_7, out=open
  // AND_Gate and_10 is placed but not wired
  // AND_Gate and_11 has open pins: in2=and_1_out, out=open
  // AND_Gate and_12 has open pins: in1=or_1_out, in3=and_3_out, out=open
  // AND_Gate and_13 is placed but not wired
  // AND_Gate and_14 is placed but not wired

  // Notes on the sheet:
  //   111
  //   000
  //   001
  //   010
  //   011
  //   100
  //   101
  //   110
endmodule
